# Fritzing sketch wiring_diagram (saved by Fritzing 0.9.6b)
circuit board: 8.46667cm x 5.64444cm
breadboards: 1

parts:
  Digispark = Digispark
  KY-023 = Black Joystick KY-023

nets:
  VCC: Digispark.VCC, KY-023.+5V
  GND: Digispark.GND, KY-023.GND
  N1: Digispark.P0, KY-023.SW
  N2: Digispark.P2, KY-023.VRx
  N3: Digispark.P5, KY-023.VRy

custom parts:
  Digispark: The Digispark is an Attiny85 based microcontroller development board similar to the Arduino line, only cheaper, smaller, and a bit less powerful. With a whole host of shields to extend its functionality and the ability to use the familiar Arduino IDE the Digispark is a great way to jump into electronics, or perfect for when an Arduino is too big or too much. May 2019 modified to correct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
  Black Joystick KY-023: Description: The joystick is a combination of 2 analoog potentiometer and a digital switch. Arduino GND --> Module pin - Arduino +5V --> Module pin +5V Arduino Analoog 0 --> Module VRx Arduino Analoog 1 --> Module VRy Arduino Digital --> Module SW Dimensions: 1" x 1.25"
