# Fritzing sketch wiring_diagram_leonardo (saved by Fritzing 0.9.6b)
circuit board: 12.6937cm x 8.57812cm
breadboards: 1

parts:
  KY-023 = Black Joystick KY-023
  Bauteil1 = Arduino Leonardo (Rev3b)

nets:
  N1: KY-023.SW, Bauteil1.D0/RX
  N2: KY-023.VRy, Bauteil1.A0
  N3: KY-023.VRx, Bauteil1.A1
  +5V: KY-023.+5V, Bauteil1.5V
  GND: KY-023.GND, Bauteil1.GND

custom parts:
  Black Joystick KY-023: Description: The joystick is a combination of 2 analoog potentiometer and a digital switch. Arduino GND --> Module pin - Arduino +5V --> Module pin +5V Arduino Analoog 0 --> Module VRx Arduino Analoog 1 --> Module VRy Arduino Digital --> Module SW Dimensions: 1" x 1.25"
